// Logisim project Es5.circ as structural Verilog: 1 circuit, main circuit main
module main (
  input  A,
  input  B,
  input  C,
  input  D
);

  // NOT_Gate not_1 is placed but not wired
  // AND_Gate and_1 is placed but not wired
  _7_Segment_Display u_7_segment_display_1 ();  // open: g, f, a, b, e, d, c, dp
endmodule
