// Logisim project Es5 (FF JK).circ as structural Verilog: 1 circuit, main circuit main
module main (
  input  in_1,
  input  in_2,
  output out_3,
  output out_4
);

  wire CLK_out, nand_1_out, nand_2_out;

  Clock #(.highDuration(2)) CLK (.out(CLK_out));
  nand nand_1 (nand_1_out, in_1, out_4, CLK_out);
  nand nand_2 (nand_2_out, in_2, out_3, CLK_out);
  nor nor_1 (out_3, nand_1_out, out_4);
  nor nor_2 (out_4, nand_2_out, out_3);
endmodule
